// Logisim project LogisimMIPSProcessor.circ as structural Verilog: 11 circuits, main circuit Main
module Main (
);

  wire alu_1_zero, ALUSrcEX, ALUSrcID, and_3_out, and_4_out, and_5_out, BranchEX, BranchID, BranchMEM,
       BranchMetEX, BranchMetMEM, BranchMetWB, Clock, control_unit_1_jal, InsertBubble, JalEX, JalID, JalMEM,
       JalWB, JrControl, JrEX, JrID, JrMEM, JumpEX, JumpID, JumpMEM, JumpWB, MemReadEX, MemReadID,
       MemReadMEM, MemtoRegEX, MemtoRegID, MemtoRegMEM, MemtoRegWB, MemWrEX, MemWrID, MemWrMEM, MemWrWB,
       NoSquashID, not_1_out, not_2_out, PCSrc, RegDstID, WrRegEX, WrRegID, WrRegMEM, WrRegWB;
  wire [1:0] forwarding_unit_1_aluselect1, forwarding_unit_1_aluselect2;
  wire [2:0] ALUCtlEX, ALUCtlID;
  wire [4:0] id_ex_1_rdaddr1out, id_ex_1_rdaddr2out, multiplexer_2_out, RdAddr1ID, RdAddr2ID, WrAddrEX,
       WrAddrID, WrAddrMEM, WrAddrWB;
  wire [5:0] func, opcode;
  wire [15:6] if_id_1_instrout;
  wire [31:0] adder_1_out, adder_2_out, alu_1_aluresult, ALUResultMEM, ALUResultWB, bit_extender_1_out,
       BranchTarget, divider_1_out, divider_2_out, divider_3_out, divider_4_out, divider_5_out,
       divider_6_out, divider_7_out, ex_mem_1_jumpaddrout, ex_mem_1_jumpfromregout, ex_mem_1_pc4offsetout,
       ex_mem_1_pc4out, ex_mem_1_rddata2out, id_ex_1_data1out, id_ex_1_data2out, id_ex_1_immeddataout,
       id_ex_1_pc4out, if_id_1_pc4out, JumpAddrEX, JumpFromRegEX, mem_wb_1_memdataout, mem_wb_1_pc4out,
       MemDataMEM, multiplexer_1_out, multiplexer_4_out, multiplexer_5_out, multiplexer_6_out,
       multiplexer_7_out, multiplexer_9_out, register_1_q, register_file_1_rddata1, register_file_1_rddata2,
       rom_1_data, shifter_1_out, WrData;

  Clock clock_1 (.out(Clock));
  Register #(.width(32)) register_1 (
    .D(multiplexer_1_out), .en(not_1_out), .Q(register_1_q), .clk(Clock));  // open: clr
  not not_1 (not_1_out, InsertBubble);
  // Probe on divider_1_out
  Divider #(.width(32)) divider_1 (.a(multiplexer_1_out), .b(32'h4), .out(divider_1_out));  // open: upper, rem
  Adder #(.width(32)) adder_1 (.a(32'h4), .b(register_1_q), .out(adder_1_out));  // open: cin, cout
  Multiplexer #(.width(32), .enable("false")) multiplexer_1 (
    .in0(adder_1_out), .in1(BranchTarget), .out(multiplexer_1_out), .sel(PCSrc));
  Divider #(.width(32)) divider_2 (.a(register_1_q), .b(32'h4), .out(divider_2_out));  // open: upper, rem
  // Probe on divider_2_out
  ROM #(.dataWidth(32)) rom_1 (.addr(register_1_q[9:2]), .data(rom_1_data));  // open: sel
  IF_ID if_id_1 (
    .InstrIn(rom_1_data), .PC4In(multiplexer_1_out), .PC4Out(if_id_1_pc4out),
    .InstrOut({opcode, RdAddr1ID, RdAddr2ID, if_id_1_instrout, func}), .CLK(Clock),
    .InsertBubble(InsertBubble));
  Control_Unit control_unit_1 (
    .opcode(opcode), .func(func), .ALUSrc(ALUSrcID), .Branch(BranchID), .Jal(control_unit_1_jal),
    .Jr(JrControl), .Jump(JumpID), .MemRead(MemReadID), .MemtoReg(MemtoRegID), .MemWr(MemWrID),
    .RegDst(RegDstID), .WrReg(WrRegID), .ALUCtl(ALUCtlID));
  Hazard_Detection hazard_detection_1 (
    .RdAddr2(RdAddr2ID), .WrAddrMEM(WrAddrMEM), .BranchMetWB(BranchMetWB), .JumpWB(JumpWB), .JumpEX(JumpEX),
    .JumpMEM(JumpMEM), .NoSquash(NoSquashID), .BranchMetEX(BranchMetEX), .BranchMetMEM(BranchMetMEM),
    .InsertBubble(InsertBubble), .RdAddr1(RdAddr1ID), .MemtoRegEX(MemtoRegEX), .WrAddrEX(WrAddrEX),
    .JrID(JrControl), .WrRegMEM(WrRegMEM));
  Multiplexer #(.width(5), .enable("false")) multiplexer_2 (
    .in0(RdAddr2ID), .in1(if_id_1_instrout[15:11]), .out(multiplexer_2_out), .sel(RegDstID));
  Divider #(.width(32)) divider_3 (.a(if_id_1_pc4out), .b(32'h4), .out(divider_3_out));  // open: upper, rem
  // Probe on divider_3_out
  Multiplexer #(.width(5), .enable("false")) multiplexer_3 (
    .in0(multiplexer_2_out), .in1({5{1'b1}}), .out(WrAddrID), .sel(JalID));
  and and_1 (JalID, NoSquashID, control_unit_1_jal);
  and and_2 (JrID, JrControl, NoSquashID);
  Register_File register_file_1 (
    .WrAddr(WrAddrWB), .WrData(WrData), .WrReg(WrRegWB), .RdAddr1(RdAddr1ID), .RdAddr2(RdAddr2ID),
    .RdData1(register_file_1_rddata1), .RdData2(register_file_1_rddata2), .Clock(not_2_out));
  not not_2 (not_2_out, Clock);
  assign bit_extender_1_out = {{16{if_id_1_instrout[15]}}, {if_id_1_instrout, func}};  // Bit_Extender bit_extender_1
  and and_3 (and_3_out, NoSquashID, JumpID);
  and and_4 (and_4_out, NoSquashID, MemWrID);
  and and_5 (and_5_out, NoSquashID, WrRegID);
  ID_EX id_ex_1 (
    .Data1In(register_file_1_rddata1), .Data1Out(id_ex_1_data1out), .Data2In(register_file_1_rddata2),
    .Data2Out(id_ex_1_data2out), .ALUSrcIn(ALUSrcID), .BranchIn(BranchID), .JalIn(JalID), .JrIn(JrID),
    .JumpIn(and_3_out), .MemReadIn(MemReadID), .MemtoRegIn(MemtoRegID), .MemWrIn(and_4_out),
    .ALUCtrlIn(ALUCtlID), .ALUSrcOut(ALUSrcEX), .BranchOut(BranchEX), .JalOut(JalEX), .JrOut(JrEX),
    .JumpOut(JumpEX), .MemReadOut(MemReadEX), .MemtoRegOut(MemtoRegEX), .MemWrOut(MemWrEX),
    .ALUCtrlOut(ALUCtlEX), .ImmedDataIn(bit_extender_1_out), .ImmedDataOut(id_ex_1_immeddataout),
    .RdAddr1In(RdAddr1ID), .RdAddr1Out(id_ex_1_rdaddr1out), .RdAddr2In(RdAddr2ID),
    .RdAddr2Out(id_ex_1_rdaddr2out), .WriteAddrD(WrAddrID), .WriteAddrEX(WrAddrEX), .WrRegOut(WrRegEX),
    .WrRegIn(and_5_out), .CLK(Clock), .PC4In(if_id_1_pc4out), .PC4Out(id_ex_1_pc4out),
    .JumpAddrIn({if_id_1_pc4out[31:28], RdAddr1ID, RdAddr2ID, if_id_1_instrout, func, 2'b00}),
    .JumpAddrOut(JumpAddrEX), .JumpFromRegIn(register_file_1_rddata1), .JumpFromRegOut(JumpFromRegEX),
    .InsertBubble(1'b0));
  Multiplexer #(.select(2), .width(32), .enable("false")) multiplexer_4 (
    .in0(id_ex_1_data1out), .in1(ALUResultMEM), .in2(WrData), .in3(MemDataMEM), .out(multiplexer_4_out),
    .sel(forwarding_unit_1_aluselect1));
  Multiplexer #(.select(2), .width(32), .enable("false")) multiplexer_5 (
    .in0(id_ex_1_data2out), .in1(ALUResultMEM), .in2(WrData), .in3(MemDataMEM), .out(multiplexer_5_out),
    .sel(forwarding_unit_1_aluselect2));
  Multiplexer #(.width(32), .enable("false")) multiplexer_6 (
    .in0(multiplexer_5_out), .in1(id_ex_1_immeddataout), .out(multiplexer_6_out), .sel(ALUSrcEX));
  // Probe on divider_4_out
  Divider #(.width(32)) divider_4 (.a(id_ex_1_pc4out), .b(32'h4), .out(divider_4_out));  // open: upper, rem
  Shifter #(.width(32)) shifter_1 (.in(id_ex_1_immeddataout), .\dist (5'b00010), .out(shifter_1_out));
  ALU alu_1 (
    .ALUCtl(ALUCtlEX), .ALUResult(alu_1_aluresult), .A(multiplexer_4_out), .B(multiplexer_6_out),
    .Zero(alu_1_zero), .Shamt(id_ex_1_immeddataout[10:6]));  // open: Overflow
  Forwarding_Unit forwarding_unit_1 (
    .RdAddr1(id_ex_1_rdaddr1out), .ALUSelect1(forwarding_unit_1_aluselect1),
    .ALUSelect2(forwarding_unit_1_aluselect2), .WrAddrMEM(WrAddrMEM), .WrRegWB(WrRegWB), .WrRegMEM(WrRegMEM),
    .WrAddrWB(WrAddrWB), .RdAddr2(id_ex_1_rdaddr2out), .MemtoRegMEM(MemtoRegMEM));
  Adder #(.width(32)) adder_2 (.a(id_ex_1_pc4out), .b(shifter_1_out), .out(adder_2_out));  // open: cin, cout
  EX_MEM ex_mem_1 (
    .BranchOut(BranchMEM), .BranchIn(BranchEX), .JalOut(JalMEM), .JalIn(JalEX), .JrOut(JrMEM), .JrIn(JrEX),
    .JumpOut(JumpMEM), .JumpIn(JumpEX), .MemReadOut(MemReadMEM), .MemReadIn(MemReadEX),
    .MemtoRegOut(MemtoRegMEM), .MemtoRegIn(MemtoRegEX), .MemWrOut(MemWrMEM), .MemWrIn(MemWrEX),
    .BranchMetMEM(BranchMetMEM), .BranchMetEX(BranchMetEX), .ALUResultIn(alu_1_aluresult),
    .ALUResultOut(ALUResultMEM), .RdData2In(multiplexer_5_out), .RdData2Out(ex_mem_1_rddata2out),
    .WriteAddrEX(WrAddrEX), .WriteAddrMEM(WrAddrMEM), .WrRegIn(WrRegEX), .WrRegOut(WrRegMEM), .CLK(Clock),
    .PC4In(id_ex_1_pc4out), .PC4Out(ex_mem_1_pc4out), .PC4OffsetIn(adder_2_out),
    .PC4OffsetOut(ex_mem_1_pc4offsetout), .JumpAddrIn(JumpAddrEX), .JumpAddrOut(ex_mem_1_jumpaddrout),
    .JumpFromRegIn(multiplexer_4_out), .JumpFromRegOut(ex_mem_1_jumpfromregout));
  and and_6 (BranchMetEX, BranchEX, alu_1_zero);
  or or_1 (PCSrc, JumpMEM, BranchMetMEM);
  // Probe on divider_5_out
  Divider #(.width(32)) divider_5 (.a(ex_mem_1_pc4out), .b(32'h4), .out(divider_5_out));  // open: upper, rem
  Multiplexer #(.width(32), .enable("false")) multiplexer_7 (
    .in0(ex_mem_1_pc4offsetout), .in1(ex_mem_1_jumpaddrout), .out(multiplexer_7_out), .sel(JumpMEM));
  Multiplexer #(.width(32), .enable("false")) multiplexer_8 (
    .in0(multiplexer_7_out), .in1(ex_mem_1_jumpfromregout), .out(BranchTarget), .sel(JrMEM));
  RAM #(.dataWidth(32), .bus("separate")) ram_1 (
    .addr(ALUResultMEM[9:2]), .din(ex_mem_1_rddata2out), .data(MemDataMEM), .str(MemWrMEM), .clk(Clock),
    .ld(MemReadMEM));  // open: sel, clr
  // Probe on divider_6_out
  Divider #(.width(32)) divider_6 (.a(BranchTarget), .b(32'h4), .out(divider_6_out));  // open: upper, rem
  MEM_WB mem_wb_1 (
    .JalOut(JalWB), .JalIn(JalMEM), .MemtoRegOut(MemtoRegWB), .MemtoRegIn(MemtoRegMEM),
    .ALUResultOut(ALUResultWB), .ALUResultIn(ALUResultMEM), .MemDataIn(MemDataMEM),
    .MemDataOut(mem_wb_1_memdataout), .WrAddrMEM(WrAddrMEM), .WrAddrWB(WrAddrWB), .WrRegIn(WrRegMEM),
    .WrRegOut(WrRegWB), .CLK(Clock), .PC4In(ex_mem_1_pc4out), .PC4Out(mem_wb_1_pc4out), .JumpIn(JumpMEM),
    .JumpOut(JumpWB), .BranchMetIn(BranchMetMEM), .BranchMetOut(BranchMetWB), .MemWrIn(MemWrMEM),
    .MemWrOut(MemWrWB));
  Divider #(.width(32)) divider_7 (.a(mem_wb_1_pc4out), .b(32'h4), .out(divider_7_out));  // open: upper, rem
  // Probe on divider_7_out
  Multiplexer #(.width(32), .enable("false")) multiplexer_9 (
    .in0(ALUResultWB), .in1(mem_wb_1_memdataout), .out(multiplexer_9_out), .sel(MemtoRegWB));
  Multiplexer #(.width(32), .enable("false")) multiplexer_10 (
    .in0(multiplexer_9_out), .in1(mem_wb_1_pc4out), .out(WrData), .sel(JalWB));

  // Notes on the sheet:
  //   Instruction Fetch
  //   contents of rom_1 (hex, n*v repeats v):
  //   34010001 211020 221826 2064000e 232824 aca4000b 8ca6000b c43824 10e10003 c7402a 11080001 201cffff
  //   20090001 8c0a000c ad4a0013 8c0a000c 1141fffb c000013 201bffff 23ff0018 ac1f0000 8c0b0000 1600008
  //   201affff 8000018 2019ffff 2018ffff
  //   Instruction Decode
  //   Execute
  //   Memory
  //   Write Back
endmodule

module ALU (
  input  [2:0] ALUCtl,
  input  [31:0] A,
  input  [31:0] B,
  input  [4:0] Shamt,
  output [31:0] ALUResult,
  output Zero,
  output Overflow
);

  wire comparator_1_lt, comparator_2_lt, comparator_3_eq, comparator_4_eq, or_2_out;
  wire [31:0] ADD, AND, NOR, OR, SLL, SLT, SLTU, SRL, SUB, XOR;

  assign XOR = A ^ B;  // XOR_Gate xor_1, 32 bits wide
  Adder #(.width(32)) adder_1 (.a(A), .b(B), .out(ADD));  // open: cin, cout
  Subtractor #(.width(32)) subtractor_1 (.a(A), .b(B), .out(SUB));  // open: bin, bout
  assign AND = A & B;  // AND_Gate and_1, 32 bits wide
  assign OR = A | B;  // OR_Gate or_1, 32 bits wide
  assign NOR = ~(A | B);  // NOR_Gate nor_1, 32 bits wide
  Comparator #(.width(32)) comparator_1 (.a(A), .b(B), .lt(comparator_1_lt));  // open: gt, eq
  assign SLT = {{31{1'b0}}, comparator_1_lt};  // Bit_Extender bit_extender_1
  Shifter #(.width(32)) shifter_1 (.in(B), .\dist (Shamt), .out(SLL));
  Shifter #(.width(32), .shift("lr")) shifter_2 (.in(B), .\dist (Shamt), .out(SRL));
  Comparator #(.width(32), .mode("unsigned")) comparator_2 (.a(A), .b(B), .lt(comparator_2_lt));  // open: gt, eq
  assign SLTU = {{31{1'b0}}, comparator_2_lt};  // Bit_Extender bit_extender_2
  Multiplexer #(.select(3), .width(32), .enable("false")) multiplexer_1 (
    .in0(AND), .in1(ADD), .in2(OR), .in3(SUB), .in4(SLT), .in5(XOR), .in6(SRL), .in7(SLL), .out(ALUResult),
    .sel(ALUCtl));
  Comparator #(.width(3)) comparator_3 (.a(3'b001), .b(ALUCtl), .eq(comparator_3_eq));  // open: gt, lt
  Comparator #(.width(3)) comparator_4 (.a(ALUCtl), .b(3'b011), .eq(comparator_4_eq));  // open: gt, lt
  Overflow_Unit overflow_unit_1 (
    .Add(comparator_3_eq), .Sub(comparator_4_eq), .ASign(A[31]), .BSign(B[31]), .ResultSign(ALUResult[31]),
    .Overflow(Overflow));
  not not_1 (Zero, or_2_out);
  or or_2 (or_2_out, ALUResult[0], ALUResult[1], ALUResult[2], ALUResult[3], ALUResult[4], ALUResult[5], ALUResult[6], ALUResult[7], ALUResult[8], ALUResult[9], ALUResult[10], ALUResult[11], ALUResult[12], ALUResult[13], ALUResult[14], ALUResult[15], ALUResult[16], ALUResult[17], ALUResult[18], ALUResult[19], ALUResult[20], ALUResult[21], ALUResult[22], ALUResult[23], ALUResult[24], ALUResult[25], ALUResult[26], ALUResult[27], ALUResult[28], ALUResult[29], ALUResult[30], ALUResult[31]);

  // Other names for the same wires on the sheet: ASign = A[31]; ResultSign = ALUResult[31]; BSign = B[31]

  // Notes on the sheet:
  //   ALUCtl for ADD on top port
  //   ALUCtl for SUB on second port
endmodule

module Register_File (
  input  [4:0] WrAddr,
  input  [31:0] WrData,
  input  WrReg,
  input  [4:0] RdAddr1,
  input  [4:0] RdAddr2,
  input  Clock,
  output [31:0] RdData1,
  output [31:0] RdData2
);

  wire WrReg0, WrReg1, WrReg2, WrReg3, WrReg4, WrReg5, WrReg6, WrReg7, WrReg8, WrReg9, WrReg10, WrReg11,
       WrReg12, WrReg13, WrReg14, WrReg15, WrReg16, WrReg17, WrReg18, WrReg19, WrReg20, WrReg21, WrReg22,
       WrReg23, WrReg24, WrReg25, WrReg26, WrReg27, WrReg28, WrReg29, WrReg30, WrReg31;
  wire [31:0] RegData1, RegData2, RegData3, RegData4, RegData5, RegData6, RegData7, RegData8, RegData9,
       RegData10, RegData11, RegData12, RegData13, RegData14, RegData15, RegData16, RegData17, RegData18,
       RegData19, RegData20, RegData21, RegData22, RegData23, RegData24, RegData25, RegData26, RegData27,
       RegData28, RegData29, RegData30, RegData31;

  Demultiplexer #(.select(5), .enable("false")) demultiplexer_1 (
    .out0(WrReg0), .out1(WrReg1), .out2(WrReg2), .out3(WrReg3), .out4(WrReg4), .out5(WrReg5), .out6(WrReg6),
    .out7(WrReg7), .out8(WrReg8), .out9(WrReg9), .out10(WrReg10), .out11(WrReg11), .out12(WrReg12),
    .out13(WrReg13), .out14(WrReg14), .out15(WrReg15), .out16(WrReg16), .out17(WrReg17), .out18(WrReg18),
    .out19(WrReg19), .out20(WrReg20), .out21(WrReg21), .out22(WrReg22), .out23(WrReg23), .out24(WrReg24),
    .out25(WrReg25), .out26(WrReg26), .out27(WrReg27), .out28(WrReg28), .out29(WrReg29), .out30(WrReg30),
    .out31(WrReg31), .in(WrReg), .sel(WrAddr));
  // Probe on RegData4
  Register #(.width(32)) Reg4 (.D(WrData), .en(WrReg4), .Q(RegData4), .clk(Clock));  // open: clr
  // Probe on RegData8
  Register #(.width(32)) Reg8 (.D(WrData), .en(WrReg8), .Q(RegData8), .clk(Clock));  // open: clr
  // Probe on RegData12
  Register #(.width(32)) Reg12 (.D(WrData), .en(WrReg12), .Q(RegData12), .clk(Clock));  // open: clr
  // Probe on RegData16
  Register #(.width(32)) Reg16 (.D(WrData), .en(WrReg16), .Q(RegData16), .clk(Clock));  // open: clr
  // Probe on RegData20
  Register #(.width(32)) Reg20 (.D(WrData), .en(WrReg20), .Q(RegData20), .clk(Clock));  // open: clr
  // Probe on RegData24
  Register #(.width(32)) Reg24 (.D(WrData), .en(WrReg24), .Q(RegData24), .clk(Clock));  // open: clr
  // Probe on RegData28
  Register #(.width(32)) Reg28 (.D(WrData), .en(WrReg28), .Q(RegData28), .clk(Clock));  // open: clr
  Register #(.width(32)) Reg1 (.D(WrData), .en(WrReg1), .Q(RegData1), .clk(Clock));  // open: clr
  Register #(.width(32)) Reg5 (.D(WrData), .en(WrReg5), .Q(RegData5), .clk(Clock));  // open: clr
  Register #(.width(32)) Reg9 (.D(WrData), .en(WrReg9), .Q(RegData9), .clk(Clock));  // open: clr
  Register #(.width(32)) Reg13 (.D(WrData), .en(WrReg13), .Q(RegData13), .clk(Clock));  // open: clr
  Register #(.width(32)) Reg17 (.D(WrData), .en(WrReg17), .Q(RegData17), .clk(Clock));  // open: clr
  Register #(.width(32)) Reg21 (.D(WrData), .en(WrReg21), .Q(RegData21), .clk(Clock));  // open: clr
  Register #(.width(32)) Reg25 (.D(WrData), .en(WrReg25), .Q(RegData25), .clk(Clock));  // open: clr
  Register #(.width(32)) Reg29 (.D(WrData), .en(WrReg29), .Q(RegData29), .clk(Clock));  // open: clr
  // Probe on RegData1
  // Probe on RegData5
  // Probe on RegData9
  // Probe on RegData13
  // Probe on RegData17
  // Probe on RegData21
  // Probe on RegData25
  // Probe on RegData29
  // Probe on RegData2
  Register #(.width(32)) Reg2 (.D(WrData), .en(WrReg2), .Q(RegData2), .clk(Clock));  // open: clr
  // Probe on RegData6
  Register #(.width(32)) Reg6 (.D(WrData), .en(WrReg6), .Q(RegData6), .clk(Clock));  // open: clr
  // Probe on RegData10
  Register #(.width(32)) Reg10 (.D(WrData), .en(WrReg10), .Q(RegData10), .clk(Clock));  // open: clr
  // Probe on RegData14
  Register #(.width(32)) Reg14 (.D(WrData), .en(WrReg14), .Q(RegData14), .clk(Clock));  // open: clr
  // Probe on RegData18
  Register #(.width(32)) Reg18 (.D(WrData), .en(WrReg18), .Q(RegData18), .clk(Clock));  // open: clr
  // Probe on RegData22
  Register #(.width(32)) Reg22 (.D(WrData), .en(WrReg22), .Q(RegData22), .clk(Clock));  // open: clr
  // Probe on RegData26
  Register #(.width(32)) Reg26 (.D(WrData), .en(WrReg26), .Q(RegData26), .clk(Clock));  // open: clr
  // Probe on RegData30
  Register #(.width(32)) Reg30 (.D(WrData), .en(WrReg30), .Q(RegData30), .clk(Clock));  // open: clr
  // Probe on RegData3
  Register #(.width(32)) Reg3 (.D(WrData), .en(WrReg3), .Q(RegData3), .clk(Clock));  // open: clr
  // Probe on RegData7
  Register #(.width(32)) Reg7 (.D(WrData), .en(WrReg7), .Q(RegData7), .clk(Clock));  // open: clr
  // Probe on RegData11
  Register #(.width(32)) Reg11 (.D(WrData), .en(WrReg11), .Q(RegData11), .clk(Clock));  // open: clr
  // Probe on RegData15
  Register #(.width(32)) Reg15 (.D(WrData), .en(WrReg15), .Q(RegData15), .clk(Clock));  // open: clr
  // Probe on RegData19
  Register #(.width(32)) Reg19 (.D(WrData), .en(WrReg19), .Q(RegData19), .clk(Clock));  // open: clr
  // Probe on RegData23
  Register #(.width(32)) Reg23 (.D(WrData), .en(WrReg23), .Q(RegData23), .clk(Clock));  // open: clr
  // Probe on RegData27
  Register #(.width(32)) Reg27 (.D(WrData), .en(WrReg27), .Q(RegData27), .clk(Clock));  // open: clr
  // Probe on RegData31
  Register #(.width(32)) Reg31 (.D(WrData), .en(WrReg31), .Q(RegData31), .clk(Clock));  // open: clr
  Multiplexer #(.select(5), .width(32), .enable("false")) multiplexer_1 (
    .in0({32{1'b0}}), .in1(RegData1), .in2(RegData2), .in3(RegData3), .in4(RegData4), .in5(RegData5),
    .in6(RegData6), .in7(RegData7), .in8(RegData8), .in9(RegData9), .in10(RegData10), .in11(RegData11),
    .in12(RegData12), .in13(RegData13), .in14(RegData14), .in15(RegData15), .in16(RegData16),
    .in17(RegData17), .in18(RegData18), .in19(RegData19), .in20(RegData20), .in21(RegData21),
    .in22(RegData22), .in23(RegData23), .in24(RegData24), .in25(RegData25), .in26(RegData26),
    .in27(RegData27), .in28(RegData28), .in29(RegData29), .in30(RegData30), .in31(RegData31), .out(RdData1),
    .sel(RdAddr1));
  Multiplexer #(.select(5), .width(32), .enable("false")) multiplexer_2 (
    .in0({32{1'b0}}), .in1(RegData1), .in2(RegData2), .in3(RegData3), .in4(RegData4), .in5(RegData5),
    .in6(RegData6), .in7(RegData7), .in8(RegData8), .in9(RegData9), .in10(RegData10), .in11(RegData11),
    .in12(RegData12), .in13(RegData13), .in14(RegData14), .in15(RegData15), .in16(RegData16),
    .in17(RegData17), .in18(RegData18), .in19(RegData19), .in20(RegData20), .in21(RegData21),
    .in22(RegData22), .in23(RegData23), .in24(RegData24), .in25(RegData25), .in26(RegData26),
    .in27(RegData27), .in28(RegData28), .in29(RegData29), .in30(RegData30), .in31(RegData31), .out(RdData2),
    .sel(RdAddr2));
endmodule

module Overflow_Unit (
  input  Add,
  input  Sub,
  input  ASign,
  input  BSign,
  input  ResultSign,
  output Overflow
);

  wire and_1_out, and_2_out, or_1_out, xnor_1_out, xor_1_out, xor_2_out;

  xnor xnor_1 (xnor_1_out, ASign, BSign);
  xor xor_1 (xor_1_out, ASign, BSign);
  and and_1 (and_1_out, xnor_1_out, Add);
  and and_2 (and_2_out, xor_1_out, Sub);
  or or_1 (or_1_out, and_1_out, and_2_out);
  xor xor_2 (xor_2_out, ResultSign, ASign);
  and and_3 (Overflow, or_1_out, xor_2_out);

  // Notes on the sheet:
  //   Overflow occurs when doing addition and sign(A) == sign(B) && sign(result) != sign(A)
  //   Or
  //   Overflow occurs when doing subtraction and sign(A) != sign(B) && sign(result) != sign(A)
endmodule

module Control_Unit (
  input  [5:0] opcode,
  input  [5:0] func,
  output ALUSrc,
  output Branch,
  output Jal,
  output Jr,
  output MemRead,
  output Jump,
  output MemtoReg,
  output MemWr,
  output RegDst,
  output WrReg,
  output [2:0] ALUCtl
);

  wire comparator_1_eq, comparator_2_eq, isJr;
  wire [2:0] rom_2_data, rom_3_data;
  wire [6:0] rom_1_data;

  Comparator #(.width(6)) comparator_1 (.a(opcode), .b({6{1'b0}}), .eq(comparator_1_eq));  // open: gt, lt
  Comparator #(.width(6)) comparator_2 (.a(6'b001000), .b(func), .eq(comparator_2_eq));  // open: gt, lt
  ROM #(.addrWidth(6), .dataWidth(10)) rom_1 (
    .addr(opcode), .data({ALUSrc, Branch, Jal, rom_1_data[6:5], MemRead, MemtoReg, MemWr, rom_1_data[1:0]}));  // open: sel
  and and_1 (isJr, comparator_1_eq, comparator_2_eq);
  ROM #(.addrWidth(6), .dataWidth(3)) rom_2 (.addr(opcode), .data(rom_2_data));  // open: sel
  ROM #(.addrWidth(6), .dataWidth(3)) rom_3 (.addr(func), .data(rom_3_data));  // open: sel
  Multiplexer #(.enable("false")) multiplexer_1 (.in0(rom_1_data[6]), .in1(1'b1), .out(Jr), .sel(isJr));
  Multiplexer #(.enable("false")) multiplexer_2 (.in0(rom_1_data[1]), .in1(1'b0), .out(RegDst), .sel(isJr));
  Multiplexer #(.enable("false")) multiplexer_3 (.in0(rom_1_data[0]), .in1(1'b0), .out(WrReg), .sel(isJr));
  or or_1 (Jump, rom_1_data[5], Jr);
  Multiplexer #(.width(3), .enable("false")) multiplexer_4 (
    .in0(rom_2_data), .in1(rom_3_data), .out(ALUCtl), .sel(comparator_1_eq));

  // Notes on the sheet:
  //   contents of rom_1 (hex, n*v repeats v):
  //   3 0 20 a1 100 0 0 0 201 0 0 0 201 201 21*0 219 7*0 204
  //   contents of rom_2 (hex, n*v repeats v):
  //   4*0 3 0 0 0 1 4*0 2 21*0 1 7*0 1
  //   contents of rom_3 (hex, n*v repeats v):
  //   7 0 6 5*0 1 23*0 1 0 3 0 0 2 5 0 0 0 4
endmodule

module IF_ID (
  input  CLK,
  input  [31:0] PC4In,
  input  [31:0] InstrIn,
  input  InsertBubble,
  output [31:0] PC4Out,
  output [31:0] InstrOut
);

  wire not_1_out;

  not not_1 (not_1_out, InsertBubble);
  Register #(.width(32)) register_1 (.D(PC4In), .en(not_1_out), .Q(PC4Out), .clk(CLK));  // open: clr
  Register #(.width(32)) register_2 (.D(InstrIn), .en(not_1_out), .Q(InstrOut), .clk(CLK));  // open: clr

  // Other names for the same wires on the sheet: Clock = CLK
endmodule

module ID_EX (
  input  CLK,
  input  [31:0] Data1In,
  input  [31:0] Data2In,
  input  [4:0] RdAddr1In,
  input  [4:0] RdAddr2In,
  input  [31:0] ImmedDataIn,
  input  [4:0] WriteAddrD,
  input  [31:0] PC4In,
  input  [31:0] JumpAddrIn,
  input  [31:0] JumpFromRegIn,
  input  InsertBubble,
  input  ALUSrcIn,
  input  BranchIn,
  input  JalIn,
  input  JrIn,
  input  JumpIn,
  input  MemReadIn,
  input  MemtoRegIn,
  input  MemWrIn,
  input  WrRegIn,
  input  [2:0] ALUCtrlIn,
  output [31:0] Data1Out,
  output [31:0] Data2Out,
  output [4:0] RdAddr1Out,
  output [4:0] RdAddr2Out,
  output [31:0] ImmedDataOut,
  output [4:0] WriteAddrEX,
  output [31:0] PC4Out,
  output [31:0] JumpAddrOut,
  output [31:0] JumpFromRegOut,
  output ALUSrcOut,
  output BranchOut,
  output JalOut,
  output JrOut,
  output JumpOut,
  output MemReadOut,
  output MemtoRegOut,
  output MemWrOut,
  output WrRegOut,
  output [2:0] ALUCtrlOut
);

  Register #(.width(32)) register_1 (.D(Data1In), .en(1'b1), .Q(Data1Out), .clk(CLK), .clr(InsertBubble));
  Register #(.width(32)) register_2 (.D(Data2In), .en(1'b1), .Q(Data2Out), .clk(CLK), .clr(InsertBubble));
  Register #(.width(5)) register_3 (.D(RdAddr1In), .en(1'b1), .Q(RdAddr1Out), .clk(CLK), .clr(InsertBubble));
  Register #(.width(5)) register_4 (.D(RdAddr2In), .en(1'b1), .Q(RdAddr2Out), .clk(CLK), .clr(InsertBubble));
  Register #(.width(32)) register_5 (.D(ImmedDataIn), .en(1'b1), .Q(ImmedDataOut), .clk(CLK), .clr(InsertBubble));
  Register #(.width(5)) register_6 (.D(WriteAddrD), .en(1'b1), .Q(WriteAddrEX), .clk(CLK), .clr(InsertBubble));
  Register #(.width(32)) register_7 (.D(PC4In), .en(1'b1), .Q(PC4Out), .clk(CLK), .clr(InsertBubble));
  Register #(.width(32)) register_8 (.D(JumpAddrIn), .en(1'b1), .Q(JumpAddrOut), .clk(CLK), .clr(InsertBubble));
  Register #(.width(32)) register_9 (.D(JumpFromRegIn), .en(1'b1), .Q(JumpFromRegOut), .clk(CLK), .clr(InsertBubble));
  Register #(.width(1)) register_10 (.D(ALUSrcIn), .en(1'b1), .Q(ALUSrcOut), .clk(CLK), .clr(InsertBubble));
  Register #(.width(1)) register_11 (.D(BranchIn), .en(1'b1), .Q(BranchOut), .clk(CLK), .clr(InsertBubble));
  Register #(.width(1)) register_12 (.D(JalIn), .en(1'b1), .Q(JalOut), .clk(CLK), .clr(InsertBubble));
  Register #(.width(1)) register_13 (.D(JrIn), .en(1'b1), .Q(JrOut), .clk(CLK), .clr(InsertBubble));
  Register #(.width(1)) register_14 (.D(JumpIn), .en(1'b1), .Q(JumpOut), .clk(CLK), .clr(InsertBubble));
  Register #(.width(1)) register_15 (.D(MemReadIn), .en(1'b1), .Q(MemReadOut), .clk(CLK), .clr(InsertBubble));
  Register #(.width(1)) register_16 (.D(MemtoRegIn), .en(1'b1), .Q(MemtoRegOut), .clk(CLK), .clr(InsertBubble));
  Register #(.width(1)) register_17 (.D(MemWrIn), .en(1'b1), .Q(MemWrOut), .clk(CLK), .clr(InsertBubble));
  Register #(.width(1)) register_18 (.D(WrRegIn), .en(1'b1), .Q(WrRegOut), .clk(CLK), .clr(InsertBubble));
  Register #(.width(3)) register_19 (.D(ALUCtrlIn), .en(1'b1), .Q(ALUCtrlOut), .clk(CLK), .clr(InsertBubble));

  // Other names for the same wires on the sheet: Clock = CLK
endmodule

module EX_MEM (
  input  CLK,
  input  BranchMetEX,
  input  [31:0] ALUResultIn,
  input  [31:0] RdData2In,
  input  [4:0] WriteAddrEX,
  input  [31:0] PC4In,
  input  [31:0] PC4OffsetIn,
  input  [31:0] JumpAddrIn,
  input  [31:0] JumpFromRegIn,
  input  BranchIn,
  input  JalIn,
  input  JrIn,
  input  JumpIn,
  input  MemReadIn,
  input  MemtoRegIn,
  input  MemWrIn,
  input  WrRegIn,
  output BranchMetMEM,
  output [31:0] ALUResultOut,
  output [31:0] RdData2Out,
  output [4:0] WriteAddrMEM,
  output [31:0] PC4Out,
  output [31:0] PC4OffsetOut,
  output [31:0] JumpAddrOut,
  output [31:0] JumpFromRegOut,
  output BranchOut,
  output JalOut,
  output JrOut,
  output JumpOut,
  output MemReadOut,
  output MemtoRegOut,
  output MemWrOut,
  output WrRegOut
);

  Register #(.width(1)) register_1 (.D(BranchMetEX), .en(1'b1), .Q(BranchMetMEM), .clk(CLK));  // open: clr
  Register #(.width(32)) register_2 (.D(ALUResultIn), .en(1'b1), .Q(ALUResultOut), .clk(CLK));  // open: clr
  Register #(.width(32)) register_3 (.D(RdData2In), .en(1'b1), .Q(RdData2Out), .clk(CLK));  // open: clr
  Register #(.width(5)) register_4 (.D(WriteAddrEX), .en(1'b1), .Q(WriteAddrMEM), .clk(CLK));  // open: clr
  Register #(.width(32)) register_5 (.D(PC4In), .en(1'b1), .Q(PC4Out), .clk(CLK));  // open: clr
  Register #(.width(32)) register_6 (.D(PC4OffsetIn), .en(1'b1), .Q(PC4OffsetOut), .clk(CLK));  // open: clr
  Register #(.width(32)) register_7 (.D(JumpAddrIn), .en(1'b1), .Q(JumpAddrOut), .clk(CLK));  // open: clr
  Register #(.width(32)) register_8 (.D(JumpFromRegIn), .en(1'b1), .Q(JumpFromRegOut), .clk(CLK));  // open: clr
  Register #(.width(1)) register_9 (.D(BranchIn), .en(1'b1), .Q(BranchOut), .clk(CLK));  // open: clr
  Register #(.width(1)) register_10 (.D(JalIn), .en(1'b1), .Q(JalOut), .clk(CLK));  // open: clr
  Register #(.width(1)) register_11 (.D(JrIn), .en(1'b1), .Q(JrOut), .clk(CLK));  // open: clr
  Register #(.width(1)) register_12 (.D(JumpIn), .en(1'b1), .Q(JumpOut), .clk(CLK));  // open: clr
  Register #(.width(1)) register_13 (.D(MemReadIn), .en(1'b1), .Q(MemReadOut), .clk(CLK));  // open: clr
  Register #(.width(1)) register_14 (.D(MemtoRegIn), .en(1'b1), .Q(MemtoRegOut), .clk(CLK));  // open: clr
  Register #(.width(1)) register_15 (.D(MemWrIn), .en(1'b1), .Q(MemWrOut), .clk(CLK));  // open: clr
  Register #(.width(1)) register_16 (.D(WrRegIn), .en(1'b1), .Q(WrRegOut), .clk(CLK));  // open: clr

  // Other names for the same wires on the sheet: Clock = CLK
endmodule

module MEM_WB (
  input  CLK,
  input  [31:0] ALUResultIn,
  input  [31:0] MemDataIn,
  input  [4:0] WrAddrMEM,
  input  [31:0] PC4In,
  input  BranchMetIn,
  input  JumpIn,
  input  JalIn,
  input  MemtoRegIn,
  input  WrRegIn,
  input  MemWrIn,
  output [31:0] ALUResultOut,
  output [31:0] MemDataOut,
  output [4:0] WrAddrWB,
  output [31:0] PC4Out,
  output BranchMetOut,
  output JumpOut,
  output JalOut,
  output MemtoRegOut,
  output WrRegOut,
  output MemWrOut
);

  Register #(.width(1)) register_1 (.D(MemWrIn), .en(1'b1), .Q(MemWrOut), .clk(CLK));  // open: clr
  Register #(.width(32)) register_2 (.D(ALUResultIn), .en(1'b1), .Q(ALUResultOut), .clk(CLK));  // open: clr
  Register #(.width(32)) register_3 (.D(MemDataIn), .en(1'b1), .Q(MemDataOut), .clk(CLK));  // open: clr
  Register #(.width(5)) register_4 (.D(WrAddrMEM), .en(1'b1), .Q(WrAddrWB), .clk(CLK));  // open: clr
  Register #(.width(32)) register_5 (.D(PC4In), .en(1'b1), .Q(PC4Out), .clk(CLK));  // open: clr
  Register #(.width(1)) register_6 (.D(BranchMetIn), .en(1'b1), .Q(BranchMetOut), .clk(CLK));  // open: clr
  Register #(.width(1)) register_7 (.D(JumpIn), .en(1'b1), .Q(JumpOut), .clk(CLK));  // open: clr
  Register #(.width(1)) register_8 (.D(JalIn), .en(1'b1), .Q(JalOut), .clk(CLK));  // open: clr
  Register #(.width(1)) register_9 (.D(MemtoRegIn), .en(1'b1), .Q(MemtoRegOut), .clk(CLK));  // open: clr
  Register #(.width(1)) register_10 (.D(WrRegIn), .en(1'b1), .Q(WrRegOut), .clk(CLK));  // open: clr

  // Other names for the same wires on the sheet: Clock = CLK
endmodule

module Forwarding_Unit (
  input  [4:0] RdAddr1,
  input  [4:0] WrAddrMEM,
  input  [4:0] WrAddrWB,
  input  WrRegWB,
  input  WrRegMEM,
  input  MemtoRegMEM,
  input  [4:0] RdAddr2,
  output [1:0] ALUSelect1,
  output [1:0] ALUSelect2
);

  wire [1:0] comparator_1_eq, comparator_3_eq;

  Comparator #(.width(5)) comparator_1 (.a(RdAddr1), .b(WrAddrMEM), .eq(comparator_1_eq[0]));  // open: gt, lt
  Comparator #(.width(5)) comparator_2 (.a(RdAddr1), .b(WrAddrWB), .eq(comparator_1_eq[1]));  // open: gt, lt
  Comparator #(.width(5)) comparator_3 (.a(RdAddr2), .b(WrAddrMEM), .eq(comparator_3_eq[0]));  // open: gt, lt
  Comparator #(.width(5)) comparator_4 (.a(RdAddr2), .b(WrAddrWB), .eq(comparator_3_eq[1]));  // open: gt, lt
  ROM #(.addrWidth(5), .dataWidth(2)) rom_1 (
    .addr({MemtoRegMEM, WrRegMEM, WrRegWB, comparator_1_eq}), .data(ALUSelect1));  // open: sel
  ROM #(.addrWidth(5), .dataWidth(2)) rom_2 (
    .addr({MemtoRegMEM, WrRegMEM, WrRegWB, comparator_3_eq}), .data(ALUSelect2));  // open: sel

  // Notes on the sheet:
  //   contents of rom_1 (hex, n*v repeats v):
  //   6*0 2 1 0 1 0 1 0 1 2 1 6*0 2 3 0 3 0 3 0 3 2 3
  //   contents of rom_2 (hex, n*v repeats v):
  //   6*0 2 1 0 1 0 1 0 1 2 1 6*0 2 3 0 3 0 3 0 3 2 3
endmodule

module Hazard_Detection (
  input  BranchMetWB,
  input  JumpWB,
  input  JumpEX,
  input  JumpMEM,
  input  BranchMetEX,
  input  BranchMetMEM,
  input  [4:0] RdAddr1,
  input  [4:0] WrAddrMEM,
  input  [4:0] RdAddr2,
  input  WrRegMEM,
  input  MemtoRegEX,
  input  [4:0] WrAddrEX,
  input  JrID,
  output NoSquash,
  output InsertBubble
);

  wire and_1_out, and_2_out, and_3_out, comparator_1_eq, comparator_2_eq, comparator_3_eq, or_1_out, or_2_out;

  Comparator #(.width(5)) comparator_1 (.a(RdAddr1), .b(WrAddrMEM), .eq(comparator_1_eq));  // open: gt, lt
  Comparator #(.width(5)) comparator_2 (.a(WrAddrMEM), .b(RdAddr2), .eq(comparator_2_eq));  // open: gt, lt
  Comparator #(.width(5)) comparator_3 (.a(WrAddrEX), .b(RdAddr1), .eq(comparator_3_eq));  // open: gt, lt
  or or_1 (or_1_out, BranchMetWB, BranchMetMEM, BranchMetEX, JumpEX, JumpMEM, JumpWB);
  and and_1 (and_1_out, comparator_1_eq, MemtoRegEX);
  and and_2 (and_2_out, comparator_2_eq, WrRegMEM, MemtoRegEX);
  and and_3 (and_3_out, comparator_3_eq, JrID);
  or or_2 (or_2_out, or_1_out, InsertBubble);
  or or_3 (InsertBubble, and_1_out, and_3_out, and_2_out);
  not not_1 (NoSquash, or_2_out);
endmodule
